// Logisim project alpha_cpu.circ as structural Verilog
module Instruction_Deoder (
  input  [4:0] in_1,
  output [7:0] out_2
);

  ROM #(.addrWidth(5)) rom_1 (.addr(in_1), .data(out_2));  // open: sel

  // Notes on the sheet:
  //   contents of rom_1 (hex, n*v repeats v):
  //   1 0 10
endmodule

module ALU (
  input  [7:0] A,
  input  [7:0] B
);
endmodule

module Registers (
  input  [7:0] R0,
  input  [7:0] R1,
  input  [7:0] R2,
  input  [7:0] R3,
  input  [7:0] R4,
  input  [7:0] R5,
  input  [7:0] R6,
  input  [7:0] R7,
  input  E,
  input  Clk,
  input  R,
  output [7:0] R0_2,
  output [7:0] R1_2,
  output [7:0] R2_2,
  output [7:0] R3_2,
  output [7:0] R4_2,
  output [7:0] R5_2,
  output [7:0] R6_2,
  output [7:0] R7_2
);

  Register register_1 (.D(R7), .en(E), .Q(R7_2), .clk(Clk), .clr(R));
  Register register_2 (.D(R6), .en(E), .Q(R6_2), .clk(Clk), .clr(R));
  Register register_3 (.D(R5), .en(E), .Q(R5_2), .clk(Clk), .clr(R));
  Register register_4 (.D(R4), .en(E), .Q(R4_2), .clk(Clk), .clr(R));
  Register register_5 (.D(R3), .en(E), .Q(R3_2), .clk(Clk), .clr(R));
  Register register_6 (.D(R2), .en(E), .Q(R2_2), .clk(Clk), .clr(R));
  Register register_7 (.D(R1), .en(E), .Q(R1_2), .clk(Clk), .clr(R));
  Register register_8 (.D(R0), .en(E), .Q(R0_2), .clk(Clk), .clr(R));
endmodule
